// Logisim project adder.circ as structural Verilog: 2 circuits, main circuit main
module main (
  input  [15:0] A,
  input  sub,
  input  [15:0] B,
  output [15:0] result,
  output ovf
);

  wire bitadder_1_cout, bitadder_2_cout, bitadder_3_cout, bitadder_4_cout, bitadder_5_cout, bitadder_6_cout,
       bitadder_7_cout, bitadder_8_cout, bitadder_9_cout, bitadder_10_cout, bitadder_11_cout,
       bitadder_12_cout, cont, s0_cout, s8_cout, s15_cout, xor_2_out, xor_3_out, xor_4_out, xor_5_out,
       xor_6_out, xor_7_out, xor_8_out, xor_9_out, xor_10_out, xor_11_out, xor_12_out, xor_13_out,
       xor_14_out, xor_15_out, xor_16_out, xor_17_out;

  xor xor_1 (ovf, bitadder_2_cout, s15_cout);
  bitadder s7 (.Cin(bitadder_1_cout), .B(xor_2_out), .A(A[7]), .sum(result[7]), .Cout(cont));
  xor xor_2 (xor_2_out, sub, B[7]);
  bitadder s15 (.Cin(bitadder_2_cout), .B(xor_3_out), .A(A[15]), .sum(result[15]), .Cout(s15_cout));
  xor xor_3 (xor_3_out, sub, B[15]);
  bitadder bitadder_1 (.Cin(bitadder_3_cout), .B(xor_4_out), .A(A[6]), .sum(result[6]), .Cout(bitadder_1_cout));
  xor xor_4 (xor_4_out, sub, B[6]);
  bitadder bitadder_2 (.Cin(bitadder_4_cout), .B(xor_5_out), .A(A[14]), .sum(result[14]), .Cout(bitadder_2_cout));
  xor xor_5 (xor_5_out, sub, B[14]);
  bitadder bitadder_3 (.Cin(bitadder_5_cout), .B(xor_6_out), .A(A[5]), .sum(result[5]), .Cout(bitadder_3_cout));
  xor xor_6 (xor_6_out, sub, B[5]);
  bitadder bitadder_4 (.Cin(bitadder_7_cout), .B(xor_7_out), .A(A[13]), .sum(result[13]), .Cout(bitadder_4_cout));
  xor xor_7 (xor_7_out, sub, B[13]);
  bitadder bitadder_5 (.Cin(bitadder_6_cout), .B(xor_8_out), .A(A[4]), .sum(result[4]), .Cout(bitadder_5_cout));
  bitadder bitadder_6 (.Cin(bitadder_9_cout), .B(xor_10_out), .A(A[3]), .sum(result[3]), .Cout(bitadder_6_cout));
  xor xor_8 (xor_8_out, sub, B[4]);
  bitadder bitadder_7 (.Cin(bitadder_8_cout), .B(xor_9_out), .A(A[12]), .sum(result[12]), .Cout(bitadder_7_cout));
  bitadder bitadder_8 (.Cin(bitadder_10_cout), .B(xor_11_out), .A(A[11]), .sum(result[11]), .Cout(bitadder_8_cout));
  xor xor_9 (xor_9_out, sub, B[12]);
  bitadder bitadder_9 (.Cin(bitadder_11_cout), .B(xor_12_out), .A(A[2]), .sum(result[2]), .Cout(bitadder_9_cout));
  xor xor_10 (xor_10_out, sub, B[3]);
  bitadder bitadder_10 (.Cin(bitadder_12_cout), .B(xor_15_out), .A(A[10]), .sum(result[10]), .Cout(bitadder_10_cout));
  xor xor_11 (xor_11_out, sub, B[11]);
  bitadder bitadder_11 (.Cin(s0_cout), .B(xor_13_out), .A(A[1]), .sum(result[1]), .Cout(bitadder_11_cout));
  xor xor_12 (xor_12_out, sub, B[2]);
  xor xor_13 (xor_13_out, sub, B[1]);
  bitadder bitadder_12 (.Cin(s8_cout), .B(xor_14_out), .A(A[9]), .sum(result[9]), .Cout(bitadder_12_cout));
  xor xor_14 (xor_14_out, sub, B[9]);
  xor xor_15 (xor_15_out, sub, B[10]);
  bitadder s0 (.Cin(sub), .B(xor_16_out), .A(A[0]), .sum(result[0]), .Cout(s0_cout));
  xor xor_16 (xor_16_out, sub, B[0]);
  bitadder s8 (.Cin(cont), .B(xor_17_out), .A(A[8]), .sum(result[8]), .Cout(s8_cout));
  xor xor_17 (xor_17_out, sub, B[8]);

  // Other names for the same wires on the sheet: A2[7:0] = A[15:8]; B2[7:0] = B[15:8]; sum1[7:0] = result[7:0];
  //   sum2[7:0] = result[15:8]
endmodule

module bitadder (
  input  Cin,
  input  B,
  input  A,
  output sum,
  output Cout
);

  wire and_1_out, and_2_out, xor_1_out;

  and and_1 (and_1_out, A, B);
  or or_1 (Cout, and_1_out, and_2_out);
  xor xor_1 (xor_1_out, B, A);
  and and_2 (and_2_out, xor_1_out, Cin);
  xor xor_2 (sum, Cin, xor_1_out);
endmodule
