// Logisim project circuit1a.circ as structural Verilog: 1 circuit, main circuit main
module main (
  input  A,
  input  B,
  input  C,
  output out
);

  or or_1 (out, A, B, C, 1'b1);
endmodule
