// Logisim project circuit1c.circ as structural Verilog: 1 circuit, main circuit main
module main (
  input  A,
  input  B,
  input  C,
  output out1,
  output out2
);

  wire and_1_out, and_2_out, and_3_out, not_1_out, not_2_out, not_3_out, not_4_out;

  not not_1 (not_1_out, A);
  not not_2 (not_2_out, B);
  not not_3 (not_3_out, C);
  and and_1 (and_1_out, not_1_out, B);
  and and_2 (and_2_out, not_2_out, C);
  and and_3 (and_3_out, A, B, not_3_out);
  not not_4 (not_4_out, C);
  and and_4 (out2, B, not_4_out);
  or or_1 (out1, and_1_out, and_2_out, and_3_out);
endmodule
