// Logisim project fsm.circ as structural Verilog: 1 circuit, main circuit main
module main (
  input  in1,
  input  in2,
  output out
);

  wire and_1_out, and_2_out, and_3_out, and_4_out, and_5_out, and_6_out, clock_1_out, D0_q, D0_qn, D1_q,
       D1_qn, not_1_out, not_2_out, not_3_out, not_4_out, not_5_out, not_6_out, or_1_out, or_2_out;

  not not_1 (not_1_out, in1);
  not not_2 (not_2_out, in2);
  not not_3 (not_3_out, in1);
  not not_4 (not_4_out, in2);
  not not_5 (not_5_out, in1);
  not not_6 (not_6_out, in2);
  and and_1 (and_1_out, D1_qn, D0_q, not_1_out, in2);
  and and_2 (and_2_out, D1_qn, D0_q, in1, not_2_out);
  and and_3 (and_3_out, D1_q, D0_qn, not_3_out, in2);
  and and_4 (and_4_out, D1_q, D0_qn, in1, not_4_out);
  and and_5 (and_5_out, D1_qn, D0_qn, not_5_out, in2);
  and and_6 (and_6_out, D1_qn, D0_qn, in1, not_6_out);
  or or_1 (or_1_out, and_5_out, and_6_out);
  D_Flip_Flop D1 (.D(or_2_out), .clk(clock_1_out), .Q(D1_q), .Qn(D1_qn));  // open: preset, reset
  or or_2 (or_2_out, and_1_out, and_2_out, and_3_out, and_4_out);
  D_Flip_Flop D0 (.D(or_1_out), .clk(clock_1_out), .Q(D0_q), .Qn(D0_qn));  // open: preset, reset
  Clock clock_1 (.out(clock_1_out));
  and and_7 (out, D1_q, D0_qn);
endmodule
