// Logisim project hw4.circ as structural Verilog: 11 circuits, main circuit main
module main (
  input  reset
);

  wire alu_2_allzero, alu_4_allzero, ALUinB, and_1_out, and_2_out, BEQ, BLT, clock_1_out, DataWE, In, JP,
       latch_oe_latched, latch_we_latched, Link, not_1_out, or_1_out, Out, Rdst, RegWE, Rwd, Sh, SL, SR;
  wire [1:0] ALUop;
  wire [2:0] multiplexer_4_out, multiplexer_5_out;
  wire [6:0] keyboard_1_data;
  wire [11:0] Address;
  wire [15:0] alu_1_aluout, alu_3_aluout, alu_4_aluout, ascii, bit_extender_1_out, bit_extender_2_out,
       data_dout, ext_extended, latch_address_latched, latch_data_in_latched, multiplexer_1_out,
       multiplexer_3_out, multiplexer_6_out, multiplexer_7_out, multiplexer_8_out, multiplexer_9_out,
       multiplexer_10_out, multiplexer_11_out, multiplexer_12_out, PC_q, registerfile_1_read2_data, rsval,
       shiftleft_1_out, shiftright_1_out;
  wire [15:12] instr_data;

  Clock clock_1 (.out(clock_1_out));
  \reg  PC (.clk(clock_1_out), .WE(1'b1), .D(multiplexer_9_out), .reset(reset), .Q(PC_q));
  Keyboard keyboard_1 (.clk(clock_1_out), .re(Out), .clr(reset), .data(keyboard_1_data));  // open: avail
  TTY #(.rows(13), .cols(80), .trigger("falling")) tty_1 (.data(rsval[6:0]), .clk(clock_1_out), .we(Out), .clr(reset));
  ROM #(.addrWidth(16), .dataWidth(16)) instr (.addr(PC_q), .data({instr_data, Address}));
  ALU alu_1 (.A(16'h1), .B(PC_q), .ALUop(2'b10), .ALUout(alu_1_aluout));  // open: allzero
  assign bit_extender_1_out = {{9{1'b0}}, keyboard_1_data};  // Bit_Extender bit_extender_1
  not not_1 (not_1_out, clock_1_out);
  ALU alu_2 (.A(bit_extender_1_out), .B(16'h80), .ALUop(2'b11), .allzero(alu_2_allzero));  // open: ALUout
  Multiplexer #(.width(16), .enable("false")) multiplexer_1 (
    .in0(multiplexer_3_out), .in1(ascii), .out(multiplexer_1_out), .sel(In));
  Multiplexer #(.width(16), .enable("false")) multiplexer_2 (
    .in0(bit_extender_1_out), .in1(16'h80), .out(ascii), .sel(alu_2_allzero));
  Multiplexer #(.width(16), .enable("false")) multiplexer_3 (
    .in0(multiplexer_12_out), .in1(alu_1_aluout), .out(multiplexer_3_out), .sel(Link));
  RegisterFile registerfile_1 (
    .write_data(multiplexer_1_out), .reset(reset), .clk(not_1_out), .WE(RegWE), .rd(multiplexer_4_out),
    .rs1(Address[11:9]), .rs2(Address[8:6]), .read1_data(rsval), .read2_data(registerfile_1_read2_data));
  Multiplexer #(.width(3), .enable("false")) multiplexer_4 (
    .in0(multiplexer_5_out), .in1(3'b111), .out(multiplexer_4_out), .sel(Link));
  Multiplexer #(.width(3), .enable("false")) multiplexer_5 (
    .in0(Address[8:6]), .in1(Address[5:3]), .out(multiplexer_5_out), .sel(Rdst));
  InstrDecode InstDecode (
    .instr(instr_data), .RegWE(RegWE), .Rdst(Rdst), .ALUinB(ALUinB), .DataWE(DataWE), .Rwd(Rwd), .BEQ(BEQ),
    .JP(JP), .ALUop(ALUop), .Link(Link), .SR(SR), .SL(SL), .Sh(Sh), .In(In), .Out(Out), .BLT(BLT));
  assign bit_extender_2_out = {{10{Address[5]}}, Address[5:0]};  // Bit_Extender bit_extender_2
  ALU alu_3 (.A(alu_1_aluout), .B(bit_extender_2_out), .ALUop(2'b10), .ALUout(alu_3_aluout));  // open: allzero
  Multiplexer #(.width(16), .enable("false")) multiplexer_6 (
    .in0(registerfile_1_read2_data), .in1(bit_extender_2_out), .out(multiplexer_6_out), .sel(ALUinB));
  RAM #(.addrWidth(16), .dataWidth(16), .trigger("high"), .databus("bibus")) data (
    .addr(latch_address_latched), .we(latch_we_latched), .oe(latch_oe_latched), .din(latch_data_in_latched),
    .dout(data_dout));
  memory_latch latch (
    .address(alu_4_aluout), .WE(DataWE), .clk(clock_1_out), .data_in(registerfile_1_read2_data),
    .address_latched(latch_address_latched), .WE_latched(latch_we_latched), .OE_latched(latch_oe_latched),
    .data_in_latched(latch_data_in_latched));
  and and_1 (and_1_out, BEQ, alu_4_allzero);
  ALU alu_4 (.A(rsval), .B(multiplexer_6_out), .ALUop(ALUop), .ALUout(alu_4_aluout), .allzero(alu_4_allzero));
  and and_2 (and_2_out, BLT, alu_4_aluout[15]);
  or or_1 (or_1_out, and_2_out, and_1_out);
  shiftRight shiftright_1 (.in(rsval), .shamt(Address[2:0]), .out(shiftright_1_out));
  Multiplexer #(.width(16), .enable("false")) multiplexer_7 (
    .in0(alu_1_aluout), .in1(alu_3_aluout), .out(multiplexer_7_out), .sel(or_1_out));
  Multiplexer #(.width(16), .enable("false")) multiplexer_8 (
    .in0(rsval), .in1(shiftright_1_out), .out(multiplexer_8_out), .sel(SR));
  shiftLeft shiftleft_1 (.in(rsval), .shamt(Address[2:0]), .out(shiftleft_1_out));
  Multiplexer #(.width(16), .enable("false")) multiplexer_9 (
    .in0(multiplexer_7_out), .in1(ext_extended), .out(multiplexer_9_out), .sel(JP));
  extend ext (.pc(alu_1_aluout), .jaddress(Address), .extended(ext_extended));
  Multiplexer #(.width(16), .enable("false")) multiplexer_10 (
    .in0(multiplexer_8_out), .in1(shiftleft_1_out), .out(multiplexer_10_out), .sel(SL));
  Multiplexer #(.width(16), .enable("false")) multiplexer_11 (
    .in0(alu_4_aluout), .in1(multiplexer_10_out), .out(multiplexer_11_out), .sel(Sh));
  Multiplexer #(.width(16), .enable("false")) multiplexer_12 (
    .in0(multiplexer_11_out), .in1(data_dout), .out(multiplexer_12_out), .sel(Rwd));

  // Other names for the same wires on the sheet: rt[2:0] = Address[8:6]; rs[2:0] = Address[11:9];
  //   Imm[5:0] = Address[5:0]; shamt[2:0] = Address[2:0]; rd[2:0] = Address[5:3]

  // Notes on the sheet:
  //   contents of instr (hex, n*v repeats v):
  //   7000 6100 6903 f008 62a0 e400 693f 313b 203f
  //   OpCode
endmodule

module \reg  (
  input  clk,
  input  WE,
  input  [15:0] D,
  input  reset,
  output [15:0] Q
);

  wire and_1_out;

  and and_1 (and_1_out, clk, WE);
  D_Flip_Flop d_ff_1 (.D(D[0]), .clk(and_1_out), .Q(Q[0]), .reset(reset));  // open: Qn, preset
  D_Flip_Flop d_ff_2 (.D(D[1]), .clk(and_1_out), .Q(Q[1]), .reset(reset));  // open: Qn, preset
  D_Flip_Flop d_ff_3 (.D(D[2]), .clk(and_1_out), .Q(Q[2]), .reset(reset));  // open: Qn, preset
  D_Flip_Flop d_ff_4 (.D(D[3]), .clk(and_1_out), .Q(Q[3]), .reset(reset));  // open: Qn, preset
  D_Flip_Flop d_ff_5 (.D(D[4]), .clk(and_1_out), .Q(Q[4]), .reset(reset));  // open: Qn, preset
  D_Flip_Flop d_ff_6 (.D(D[5]), .clk(and_1_out), .Q(Q[5]), .reset(reset));  // open: Qn, preset
  D_Flip_Flop d_ff_7 (.D(D[6]), .clk(and_1_out), .Q(Q[6]), .reset(reset));  // open: Qn, preset
  D_Flip_Flop d_ff_8 (.D(D[7]), .clk(and_1_out), .Q(Q[7]), .reset(reset));  // open: Qn, preset
  D_Flip_Flop d_ff_9 (.D(D[8]), .clk(and_1_out), .Q(Q[8]), .reset(reset));  // open: Qn, preset
  D_Flip_Flop d_ff_10 (.D(D[9]), .clk(and_1_out), .Q(Q[9]), .reset(reset));  // open: Qn, preset
  D_Flip_Flop d_ff_11 (.D(D[10]), .clk(and_1_out), .Q(Q[10]), .reset(reset));  // open: Qn, preset
  D_Flip_Flop d_ff_12 (.D(D[11]), .clk(and_1_out), .Q(Q[11]), .reset(reset));  // open: Qn, preset
  D_Flip_Flop d_ff_13 (.D(D[12]), .clk(and_1_out), .Q(Q[12]), .reset(reset));  // open: Qn, preset
  D_Flip_Flop d_ff_14 (.D(D[13]), .clk(and_1_out), .Q(Q[13]), .reset(reset));  // open: Qn, preset
  D_Flip_Flop d_ff_15 (.D(D[14]), .clk(and_1_out), .Q(Q[14]), .reset(reset));  // open: Qn, preset
  D_Flip_Flop d_ff_16 (.D(D[15]), .clk(and_1_out), .Q(Q[15]), .reset(reset));  // open: Qn, preset
endmodule

module RegisterFile (
  input  [15:0] write_data,
  input  reset,
  input  clk,
  input  WE,
  input  [2:0] rd,
  input  [2:0] rs1,
  input  [2:0] rs2,
  output [15:0] read1_data,
  output [15:0] read2_data
);

  wire and_1_out, and_2_out, and_3_out, and_4_out, and_5_out, and_6_out, and_7_out, decoder_1_out1,
       decoder_1_out2, decoder_1_out3, decoder_1_out4, decoder_1_out5, decoder_1_out6, decoder_1_out7,
       decoder_2_out0, decoder_2_out1, decoder_2_out2, decoder_2_out3, decoder_2_out4, decoder_2_out5,
       decoder_2_out6, decoder_2_out7, decoder_3_out0, decoder_3_out1, decoder_3_out2, decoder_3_out3,
       decoder_3_out4, decoder_3_out5, decoder_3_out6, decoder_3_out7;
  wire [15:0] r0_2_q, r1_2_q, r2_2_q, r3_2_q, r4_2_q, r5_2_q, r6_2_q, r7_2_q;

  Decoder #(.select(3)) decoder_1 (
    .out1(decoder_1_out1), .out2(decoder_1_out2), .out3(decoder_1_out3), .out4(decoder_1_out4),
    .out5(decoder_1_out5), .out6(decoder_1_out6), .out7(decoder_1_out7), .sel(rd));  // open: out0, en
  // Probe on r0_2_q
  \reg  r0_2 (.clk(clk), .WE(1'b0), .D(write_data), .reset(reset), .Q(r0_2_q));
  // Probe on r1_2_q
  \reg  r1_2 (.clk(clk), .WE(and_1_out), .D(write_data), .reset(reset), .Q(r1_2_q));
  and and_1 (and_1_out, WE, decoder_1_out1);
  // Probe on r2_2_q
  \reg  r2_2 (.clk(clk), .WE(and_2_out), .D(write_data), .reset(reset), .Q(r2_2_q));
  and and_2 (and_2_out, WE, decoder_1_out2);
  // Probe on r3_2_q
  \reg  r3_2 (.clk(clk), .WE(and_3_out), .D(write_data), .reset(reset), .Q(r3_2_q));
  and and_3 (and_3_out, WE, decoder_1_out3);
  // Probe on r4_2_q
  \reg  r4_2 (.clk(clk), .WE(and_4_out), .D(write_data), .reset(reset), .Q(r4_2_q));
  and and_4 (and_4_out, WE, decoder_1_out4);
  // Probe on r5_2_q
  \reg  r5_2 (.clk(clk), .WE(and_5_out), .D(write_data), .reset(reset), .Q(r5_2_q));
  and and_5 (and_5_out, WE, decoder_1_out5);
  // Probe on r6_2_q
  \reg  r6_2 (.clk(clk), .WE(and_6_out), .D(write_data), .reset(reset), .Q(r6_2_q));
  and and_6 (and_6_out, WE, decoder_1_out6);
  // Probe on r7_2_q
  \reg  r7_2 (.clk(clk), .WE(and_7_out), .D(write_data), .reset(reset), .Q(r7_2_q));
  and and_7 (and_7_out, WE, decoder_1_out7);
  Decoder #(.select(3)) decoder_2 (
    .out0(decoder_2_out0), .out1(decoder_2_out1), .out2(decoder_2_out2), .out3(decoder_2_out3),
    .out4(decoder_2_out4), .out5(decoder_2_out5), .out6(decoder_2_out6), .out7(decoder_2_out7), .sel(rs1));  // open: en
  assign read1_data = decoder_2_out0 ? r0_2_q : 16'bz;  // Controlled_Buffer controlled_buffer_1
  assign read1_data = decoder_2_out1 ? r1_2_q : 16'bz;  // Controlled_Buffer controlled_buffer_2
  assign read1_data = decoder_2_out2 ? r2_2_q : 16'bz;  // Controlled_Buffer controlled_buffer_3
  assign read1_data = decoder_2_out3 ? r3_2_q : 16'bz;  // Controlled_Buffer controlled_buffer_4
  assign read1_data = decoder_2_out4 ? r4_2_q : 16'bz;  // Controlled_Buffer controlled_buffer_5
  assign read1_data = decoder_2_out5 ? r5_2_q : 16'bz;  // Controlled_Buffer controlled_buffer_6
  assign read1_data = decoder_2_out6 ? r6_2_q : 16'bz;  // Controlled_Buffer controlled_buffer_7
  assign read1_data = decoder_2_out7 ? r7_2_q : 16'bz;  // Controlled_Buffer controlled_buffer_8
  assign read2_data = decoder_3_out0 ? r0_2_q : 16'bz;  // Controlled_Buffer controlled_buffer_9
  assign read2_data = decoder_3_out1 ? r1_2_q : 16'bz;  // Controlled_Buffer controlled_buffer_10
  Decoder #(.select(3)) decoder_3 (
    .out0(decoder_3_out0), .out1(decoder_3_out1), .out2(decoder_3_out2), .out3(decoder_3_out3),
    .out4(decoder_3_out4), .out5(decoder_3_out5), .out6(decoder_3_out6), .out7(decoder_3_out7), .sel(rs2));  // open: en
  assign read2_data = decoder_3_out2 ? r2_2_q : 16'bz;  // Controlled_Buffer controlled_buffer_11
  assign read2_data = decoder_3_out3 ? r3_2_q : 16'bz;  // Controlled_Buffer controlled_buffer_12
  assign read2_data = decoder_3_out4 ? r4_2_q : 16'bz;  // Controlled_Buffer controlled_buffer_13
  assign read2_data = decoder_3_out5 ? r5_2_q : 16'bz;  // Controlled_Buffer controlled_buffer_14
  assign read2_data = decoder_3_out6 ? r6_2_q : 16'bz;  // Controlled_Buffer controlled_buffer_15
  assign read2_data = decoder_3_out7 ? r7_2_q : 16'bz;  // Controlled_Buffer controlled_buffer_16
endmodule

module bitadder (
  input  Cin,
  input  B,
  input  A,
  output sum,
  output Cout
);

  wire and_1_out, and_2_out, xor_1_out;

  and and_1 (and_1_out, A, B);
  or or_1 (Cout, and_1_out, and_2_out);
  xor xor_1 (xor_1_out, B, A);
  and and_2 (and_2_out, xor_1_out, Cin);
  xor xor_2 (sum, Cin, xor_1_out);
endmodule

module addersixteen (
  input  [15:0] A,
  input  sub,
  input  [15:0] B,
  output [15:0] result
);

  wire bitadder_3_cout, bitadder_4_cout, bitadder_5_cout, bitadder_6_cout, bitadder_7_cout, bitadder_8_cout,
       bitadder_9_cout, bitadder_10_cout, bitadder_11_cout, bitadder_12_cout, bitadder_13_cout,
       bitadder_14_cout, bitadder_15_cout, bitadder_16_cout, cont, xor_1_out, xor_2_out, xor_3_out,
       xor_4_out, xor_5_out, xor_6_out, xor_7_out, xor_8_out, xor_9_out, xor_10_out, xor_11_out, xor_12_out,
       xor_13_out, xor_14_out, xor_15_out, xor_16_out;

  bitadder bitadder_1 (.Cin(bitadder_3_cout), .B(xor_1_out), .A(A[7]), .sum(result[7]), .Cout(cont));
  xor xor_1 (xor_1_out, sub, B[7]);
  bitadder bitadder_2 (.Cin(bitadder_4_cout), .B(xor_2_out), .A(A[15]), .sum(result[15]));  // open: Cout
  xor xor_2 (xor_2_out, sub, B[15]);
  bitadder bitadder_3 (.Cin(bitadder_5_cout), .B(xor_3_out), .A(A[6]), .sum(result[6]), .Cout(bitadder_3_cout));
  xor xor_3 (xor_3_out, sub, B[6]);
  bitadder bitadder_4 (.Cin(bitadder_6_cout), .B(xor_4_out), .A(A[14]), .sum(result[14]), .Cout(bitadder_4_cout));
  xor xor_4 (xor_4_out, sub, B[14]);
  bitadder bitadder_5 (.Cin(bitadder_8_cout), .B(xor_5_out), .A(A[5]), .sum(result[5]), .Cout(bitadder_5_cout));
  xor xor_5 (xor_5_out, sub, B[5]);
  bitadder bitadder_6 (.Cin(bitadder_10_cout), .B(xor_6_out), .A(A[13]), .sum(result[13]), .Cout(bitadder_6_cout));
  xor xor_6 (xor_6_out, sub, B[13]);
  bitadder bitadder_7 (.Cin(bitadder_11_cout), .B(xor_9_out), .A(A[3]), .sum(result[3]), .Cout(bitadder_7_cout));
  bitadder bitadder_8 (.Cin(bitadder_7_cout), .B(xor_7_out), .A(A[4]), .sum(result[4]), .Cout(bitadder_8_cout));
  xor xor_7 (xor_7_out, sub, B[4]);
  bitadder bitadder_9 (.Cin(bitadder_12_cout), .B(xor_10_out), .A(A[11]), .sum(result[11]), .Cout(bitadder_9_cout));
  bitadder bitadder_10 (.Cin(bitadder_9_cout), .B(xor_8_out), .A(A[12]), .sum(result[12]), .Cout(bitadder_10_cout));
  xor xor_8 (xor_8_out, sub, B[12]);
  bitadder bitadder_11 (.Cin(bitadder_13_cout), .B(xor_11_out), .A(A[2]), .sum(result[2]), .Cout(bitadder_11_cout));
  xor xor_9 (xor_9_out, sub, B[3]);
  bitadder bitadder_12 (.Cin(bitadder_14_cout), .B(xor_13_out), .A(A[10]), .sum(result[10]), .Cout(bitadder_12_cout));
  xor xor_10 (xor_10_out, sub, B[11]);
  bitadder bitadder_13 (.Cin(bitadder_15_cout), .B(xor_12_out), .A(A[1]), .sum(result[1]), .Cout(bitadder_13_cout));
  xor xor_11 (xor_11_out, sub, B[2]);
  xor xor_12 (xor_12_out, sub, B[1]);
  bitadder bitadder_14 (.Cin(bitadder_16_cout), .B(xor_14_out), .A(A[9]), .sum(result[9]), .Cout(bitadder_14_cout));
  xor xor_13 (xor_13_out, sub, B[10]);
  xor xor_14 (xor_14_out, sub, B[9]);
  bitadder bitadder_15 (.Cin(sub), .B(xor_15_out), .A(A[0]), .sum(result[0]), .Cout(bitadder_15_cout));
  xor xor_15 (xor_15_out, sub, B[0]);
  bitadder bitadder_16 (.Cin(cont), .B(xor_16_out), .A(A[8]), .sum(result[8]), .Cout(bitadder_16_cout));
  xor xor_16 (xor_16_out, sub, B[8]);

  // Other names for the same wires on the sheet: A2[7:0] = A[15:8]; B2[7:0] = B[15:8]; sum1[7:0] = result[7:0];
  //   sum2[7:0] = result[15:8]
endmodule

module ALU (
  input  [15:0] A,
  input  [15:0] B,
  input  [1:0] ALUop,
  output [15:0] ALUout,
  output allzero
);

  wire [15:0] addersixteen_1_result, addersixteen_2_result, and_1_out, or_1_out;

  assign and_1_out = B & A;  // AND_Gate and_1, 16 bits wide
  assign or_1_out = B | A;  // OR_Gate or_1, 16 bits wide
  addersixteen addersixteen_1 (.A(A), .sub(1'b0), .B(B), .result(addersixteen_1_result));
  addersixteen addersixteen_2 (.A(A), .sub(1'b1), .B(B), .result(addersixteen_2_result));
  Multiplexer #(.select(2), .width(16), .enable("false")) multiplexer_1 (
    .in0(and_1_out), .in1(or_1_out), .in2(addersixteen_1_result), .in3(addersixteen_2_result), .out(ALUout),
    .sel(ALUop));
  nor nor_1 (allzero, ALUout[0], ALUout[1], ALUout[2], ALUout[3], ALUout[4], ALUout[5], ALUout[6], ALUout[7], ALUout[9], ALUout[10], ALUout[11], ALUout[12], ALUout[13], ALUout[14], ALUout[15], ALUout[8]);

  // Notes on the sheet:
  //   Currently: 00-AND, 01-OR, 10-add, 11-sub
endmodule

module InstrDecode (
  input  [3:0] instr,
  output RegWE,
  output Rdst,
  output ALUinB,
  output DataWE,
  output Rwd,
  output BEQ,
  output JP,
  output [1:0] ALUop,
  output Link,
  output SR,
  output SL,
  output Sh,
  output In,
  output Out,
  output BLT
);

  wire add, addi, \and , beq_t, j, \or , sub, subi;

  Decoder #(.select(4)) decoder_1 (
    .out0(Rwd), .out1(DataWE), .out2(beq_t), .out3(BLT), .out4(\or ), .out5(\and ), .out6(addi), .out7(add),
    .out8(sub), .out9(subi), .out10(SR), .out11(SL), .out12(j), .out13(Link), .out14(Out), .out15(In),
    .sel(instr));  // open: en
  or or_1 (RegWE, SL, SR, \or , add, Rwd, In, \and , addi, Link, sub, subi);
  or or_2 (Rdst, In, sub, add, \or , \and , SR, SL);
  or or_3 (ALUinB, addi, DataWE, Rwd, subi);
  buf or_4 (BEQ, beq_t);  // OR_Gate
  or or_5 (JP, Link, j);
  or or_6 (ALUop[1], sub, add, Rwd, beq_t, BLT, DataWE, addi, subi);
  or or_7 (ALUop[0], beq_t, sub, BLT, subi, \or );
  or or_8 (Sh, SR, SL);

  // Other names for the same wires on the sheet: input = In; jal = Link; lw = Rwd; output = Out; shl = SL; shr = SR;
  //   sw = DataWE
endmodule

module memory_latch (
  input  [15:0] address,
  input  WE,
  input  clk,
  input  [15:0] data_in,
  output [15:0] address_latched,
  output WE_latched,
  output OE_latched,
  output [15:0] data_in_latched
);

  wire d_ff_1_q;
  wire [15:0] register_1_q;

  Register #(.width(16), .trigger("falling")) register_1 (
    .D(address), .en(WE), .clk(clk), .Q(register_1_q));  // open: clr
  D_Flip_Flop #(.trigger("falling")) d_ff_1 (.D(WE), .clk(clk), .Q(d_ff_1_q));  // open: Qn, preset, reset
  Register #(.width(16), .trigger("falling")) register_2 (
    .D(data_in), .en(WE), .clk(clk), .Q(data_in_latched));  // open: clr
  Multiplexer #(.width(16), .enable("false")) multiplexer_1 (
    .in0(address), .in1(register_1_q), .out(address_latched), .sel(d_ff_1_q));
  and and_1 (WE_latched, clk, d_ff_1_q);
  not not_1 (OE_latched, WE_latched);
endmodule

module extend (
  input  [15:0] pc,
  input  [11:0] jaddress,
  output [15:0] extended
);


  assign extended = {pc[15:12], jaddress};
endmodule

module shiftRight (
  input  [15:0] in,
  input  [2:0] shamt,
  output [15:0] out
);

  wire [15:0] multiplexer_1_out, multiplexer_2_out;

  Multiplexer #(.width(16), .enable("false")) multiplexer_1 (
    .in0(in), .in1({1'b0, in[15:1]}), .out(multiplexer_1_out), .sel(shamt[0]));
  Multiplexer #(.width(16), .enable("false")) multiplexer_2 (
    .in0(multiplexer_1_out), .in1({2'b00, multiplexer_1_out[15:2]}), .out(multiplexer_2_out), .sel(shamt[1]));
  Multiplexer #(.width(16), .enable("false")) multiplexer_3 (
    .in0(multiplexer_2_out), .in1({4'b0000, multiplexer_2_out[15:4]}), .out(out), .sel(shamt[2]));
endmodule

module shiftLeft (
  input  [15:0] in,
  input  [2:0] shamt,
  output [15:0] out
);

  wire [15:0] multiplexer_1_out, multiplexer_2_out;

  Multiplexer #(.width(16), .enable("false")) multiplexer_1 (
    .in0(in), .in1({in[14:0], 1'b0}), .out(multiplexer_1_out), .sel(shamt[0]));
  Multiplexer #(.width(16), .enable("false")) multiplexer_2 (
    .in0(multiplexer_1_out), .in1({multiplexer_1_out[13:0], 2'b00}), .out(multiplexer_2_out), .sel(shamt[1]));
  Multiplexer #(.width(16), .enable("false")) multiplexer_3 (
    .in0(multiplexer_2_out), .in1({multiplexer_2_out[11:0], 4'b0000}), .out(out), .sel(shamt[2]));
endmodule
